// Logisim project ep4.circ as structural Verilog: 2 circuits, main circuit main
module main (
);

  wire cl, clock_1_out, controlador_1_lda__11, controlador_1_nop__50, controlador_1_sta__12, d_ff_1_qn, JMP,
       not_1_out, or_1_out, STP, xor_1_out;
  wire [7:0] counter_1_q, \Endereço , multiplexer_1_out;
  wire [15:0] ACC, demultiplexer_1_out0, demultiplexer_1_out1, ram_1_data;
  wire [15:8] register_1_q;

  Clock #(.highDuration(2), .lowDuration(2)) clock_1 (.out(clock_1_out));
  D_Flip_Flop d_ff_1 (.clk(clock_1_out), .Qn(d_ff_1_qn));  // open: D, Q, preset, en, reset
  not not_1 (not_1_out, clock_1_out);
  Clock clock_2 (.out(cl));
  ExactlyOne xor_1 (.out(xor_1_out), .in0(JMP), .in1(STP), .in2(d_ff_1_qn));
  Counter counter_1 (
    .load(JMP), .D(\Endereço ), .count(xor_1_out), .Q(counter_1_q), .clk(not_1_out));  // open: carry, clr
  or or_1 (or_1_out, controlador_1_sta__12, controlador_1_lda__11);
  Multiplexer #(.width(8), .enable("false")) multiplexer_1 (
    .in0(counter_1_q), .in1(\Endereço ), .out(multiplexer_1_out), .sel(or_1_out));
  RAM #(.dataWidth(16), .bus("separate")) ram_1 (
    .addr(multiplexer_1_out), .din(ACC), .data(ram_1_data), .str(controlador_1_sta__12), .clk(cl));  // open: sel, ld, clr
  Demultiplexer #(.width(16), .enable("false")) demultiplexer_1 (
    .out0(demultiplexer_1_out0), .out1(demultiplexer_1_out1), .in(ram_1_data), .sel(controlador_1_lda__11));
  LED NOP (.in(controlador_1_nop__50));
  // Probe on register_1_q
  Controlador controlador_1 (
    .\Instrução (register_1_q), .LDA__11(controlador_1_lda__11), .STA__12(controlador_1_sta__12),
    .NOP__50(controlador_1_nop__50), .JMP__51(JMP), .STP__70(STP));
  Register #(.width(16)) register_1 (
    .D(demultiplexer_1_out0), .Q({register_1_q, \Endereço }), .clk(cl));  // open: en, clr
  // Probe on \Endereço 
  // Probe on demultiplexer_1_out1
  Register #(.width(16), .trigger("falling")) register_2 (
    .D(demultiplexer_1_out1), .en(controlador_1_lda__11), .Q(ACC), .clk(cl));  // open: clr

  // Notes on the sheet:
  //   > Daniel Toshio Iwamoto      - nº USP: 8516782
  //   > Gustavo Chicato Wandeur - nº USP: 7557797
  //   > Leonardo Pereira Macedo - nº USP: 8536065
  //   Componentes do grupo:
  //   PC (Program Counter)
  //   EP3 - Algebra Booleana
  //   Professor: Junior Barrera
  //   Memória
  //   IR (Instruction Register)
  //   Acumulador
endmodule

module Controlador (
  input  [7:0] \Instrução ,
  output LDA__11,
  output STA__12,
  output NOP__50,
  output JMP__51,
  output STP__70
);

  wire _0_L, _2_R, _3_L, _3_R, _4_L, _6_R, B_R, C_R;

  and and_1 (LDA__11, _0_L, B_R);
  Decoder #(.select(4), .enable("false")) decoder_1 (
    .out0(_0_L), .out3(_3_L), .out4(_4_L), .sel(\Instrução [7:4]));  // open: out1, out2, out5, out6, out7, out8, out9, out10, out11, out12, out13, out14, out15
  and and_2 (STA__12, _0_L, C_R);
  and and_3 (NOP__50, _3_L, _2_R);
  Decoder #(.select(4), .enable("false")) decoder_2 (
    .out2(_2_R), .out3(_3_R), .out6(_6_R), .out11(B_R), .out12(C_R), .sel(\Instrução [3:0]));  // open: out0, out1, out4, out5, out7, out8, out9, out10, out13, out14, out15
  and and_4 (JMP__51, _3_L, _3_R);
  and and_5 (STP__70, _4_L, _6_R);

  // Notes on the sheet:
  //   4 bits mais significativos
  //   Análise da instrução
  //   4 bits menos significativos
endmodule
